// Logisim project Keypad.circ as structural Verilog: 1 circuit, main circuit main
module main (
  input  _7,
  input  _8,
  input  _9,
  input  _4,
  input  _5,
  input  _6,
  input  _1,
  input  _2,
  input  _3,
  input  _0,
  input  in_11,
  input  in_12,
  input  in_13,
  input  in_14,
  output [7:0] out_15
);

  wire Active_out, and_1_out, clock_1_out, not_1_out, not_2_out, not_3_out, not_4_out, or_1_out, or_2_out,
       or_3_out, or_4_out;

  or Active (Active_out, _9, _8, _7, _6, _5, _4, _3, _2, _1, _0);
  Clock clock_1 (.out(clock_1_out));
  or or_1 (or_1_out, _1, _3, _5, _7, _9);
  not not_1 (not_1_out, or_1_out);
  and and_1 (and_1_out, Active_out, clock_1_out);
  S_R_Flip_Flop s_r_ff_1 (.S(or_1_out), .clk(and_1_out), .R(not_1_out), .Q(out_15[0]));  // open: Qn, preset, reset, en
  or or_2 (or_2_out, _2, _3, _6, _7);
  S_R_Flip_Flop s_r_ff_2 (.S(or_2_out), .clk(and_1_out), .R(not_2_out), .Q(out_15[1]));  // open: Qn, preset, reset, en
  not not_2 (not_2_out, or_2_out);
  // Probe on {in_14, in_13, in_12, in_11, out_15[3:0]}
  or or_3 (or_3_out, _4, _5, _6, _7);
  not not_3 (not_3_out, or_3_out);
  S_R_Flip_Flop s_r_ff_3 (.S(or_3_out), .clk(and_1_out), .R(not_3_out), .Q(out_15[2]));  // open: Qn, preset, reset, en
  or or_4 (or_4_out, _8, _9);
  S_R_Flip_Flop s_r_ff_4 (.S(or_4_out), .clk(and_1_out), .R(not_4_out), .Q(out_15[3]));  // open: Qn, preset, reset, en
  not not_4 (not_4_out, or_4_out);

  assign out_15[7:4] = {in_14, in_13, in_12, in_11};
endmodule
