// Logisim project MBREvo.circ as structural Verilog: 2 circuits, main circuit MBR
module MBR (
  input  [7:0] In_1,
  input  [7:0] In_0,
  input  InMode,
  input  InOn,
  input  OutOn,
  input  Clock,
  output [7:0] Out_0,
  output [7:0] Out_1,
  output [7:0] Contents
);

  wire and_1_out, and_2_out, and_3_out, and_4_out, and_5_out, and_6_out, and_7_out, and_8_out, and_9_out,
       and_10_out, and_11_out, and_12_out, and_13_out, and_14_out, and_15_out, and_16_out, and_17_out,
       not_1_out, not_2_out, not_3_out, not_4_out, not_5_out, not_6_out, not_7_out, not_8_out, not_9_out,
       not_10_out, not_11_out, not_12_out, not_13_out, not_14_out, not_15_out, not_16_out, not_17_out,
       or_1_out, or_2_out, or_3_out, or_4_out, or_5_out, or_6_out, or_7_out, or_8_out;

  and and_1 (and_1_out, InOn, Clock);
  and and_2 (and_2_out, In_1[0], InMode);
  and and_3 (and_3_out, In_1[1], InMode);
  and and_4 (and_4_out, In_1[2], InMode);
  and and_5 (and_5_out, In_1[3], InMode);
  and and_6 (and_6_out, In_1[4], InMode);
  and and_7 (and_7_out, In_1[5], InMode);
  and and_8 (and_8_out, In_1[6], InMode);
  and and_9 (and_9_out, In_1[7], InMode);
  not not_1 (not_1_out, InMode);
  and and_10 (and_10_out, In_0[0], not_1_out);
  and and_11 (and_11_out, In_0[1], not_1_out);
  and and_12 (and_12_out, In_0[2], not_1_out);
  and and_13 (and_13_out, In_0[3], not_1_out);
  and and_14 (and_14_out, In_0[4], not_1_out);
  and and_15 (and_15_out, In_0[5], not_1_out);
  and and_16 (and_16_out, In_0[6], not_1_out);
  and and_17 (and_17_out, In_0[7], not_1_out);
  S_R_Flip_Flop s_r_ff_1 (.S(or_1_out), .R(not_2_out), .clk(and_1_out), .Q(Contents[0]));  // open: reset, Qn, preset
  or or_1 (or_1_out, and_2_out, and_10_out);
  not not_2 (not_2_out, or_1_out);
  or or_2 (or_2_out, and_3_out, and_11_out);
  S_R_Flip_Flop s_r_ff_2 (.S(or_2_out), .R(not_3_out), .clk(and_1_out), .Q(Contents[1]));  // open: reset, Qn, preset
  not not_3 (not_3_out, or_2_out);
  S_R_Flip_Flop s_r_ff_3 (.S(or_3_out), .R(not_4_out), .clk(and_1_out), .Q(Contents[2]));  // open: reset, Qn, preset
  or or_3 (or_3_out, and_4_out, and_12_out);
  not not_4 (not_4_out, or_3_out);
  or or_4 (or_4_out, and_5_out, and_13_out);
  S_R_Flip_Flop s_r_ff_4 (.S(or_4_out), .R(not_5_out), .clk(and_1_out), .Q(Contents[3]));  // open: reset, Qn, preset
  not not_5 (not_5_out, or_4_out);
  S_R_Flip_Flop s_r_ff_5 (.S(or_5_out), .R(not_6_out), .clk(and_1_out), .Q(Contents[4]));  // open: reset, Qn, preset
  or or_5 (or_5_out, and_6_out, and_14_out);
  not not_6 (not_6_out, or_5_out);
  or or_6 (or_6_out, and_7_out, and_15_out);
  S_R_Flip_Flop s_r_ff_6 (.S(or_6_out), .R(not_7_out), .clk(and_1_out), .Q(Contents[5]));  // open: reset, Qn, preset
  not not_7 (not_7_out, or_6_out);
  S_R_Flip_Flop s_r_ff_7 (.S(or_7_out), .R(not_8_out), .clk(and_1_out), .Q(Contents[6]));  // open: reset, Qn, preset
  or or_7 (or_7_out, and_8_out, and_16_out);
  not not_8 (not_8_out, or_7_out);
  or or_8 (or_8_out, and_9_out, and_17_out);
  S_R_Flip_Flop s_r_ff_8 (.S(or_8_out), .R(not_9_out), .clk(and_1_out), .Q(Contents[7]));  // open: reset, Qn, preset
  not not_9 (not_9_out, or_8_out);
  not not_10 (not_10_out, InMode);
  not not_11 (not_11_out, InMode);
  not not_12 (not_12_out, InMode);
  not not_13 (not_13_out, InMode);
  not not_14 (not_14_out, InMode);
  not not_15 (not_15_out, InMode);
  not not_16 (not_16_out, InMode);
  not not_17 (not_17_out, InMode);
  and and_18 (Out_0[0], Contents[0], OutOn, not_10_out);
  and and_19 (Out_0[1], Contents[1], OutOn, not_11_out);
  and and_20 (Out_0[2], Contents[2], OutOn, not_12_out);
  and and_21 (Out_0[3], Contents[3], OutOn, not_13_out);
  and and_22 (Out_0[4], Contents[4], OutOn, not_14_out);
  and and_23 (Out_0[5], Contents[5], OutOn, not_15_out);
  and and_24 (Out_0[6], Contents[6], OutOn, not_16_out);
  and and_25 (Out_0[7], Contents[7], OutOn, not_17_out);
  and and_26 (Out_1[0], Contents[0], OutOn, InMode);
  and and_27 (Out_1[1], Contents[1], OutOn, InMode);
  and and_28 (Out_1[2], Contents[2], OutOn, InMode);
  and and_29 (Out_1[3], Contents[3], OutOn, InMode);
  and and_30 (Out_1[4], Contents[4], OutOn, InMode);
  and and_31 (Out_1[5], Contents[5], OutOn, InMode);
  and and_32 (Out_1[6], Contents[6], OutOn, InMode);
  and and_33 (Out_1[7], Contents[7], OutOn, InMode);
endmodule

module main (
  input  [7:0] in_1,
  input  [7:0] in_2,
  input  in_3,
  input  in_4,
  input  in_5,
  output [7:0] out_6,
  output [7:0] out_7,
  output [7:0] out_8
);

  wire clock_1_out;

  Clock clock_1 (.out(clock_1_out));
  MBR mbr_1 (
    .In_1(in_1), .In_0(in_2), .InMode(in_3), .InOn(in_4), .OutOn(in_5), .Clock(clock_1_out), .Out_0(out_6),
    .Out_1(out_7), .Contents(out_8));
endmodule
